// Logisim project TBX32.circ as structural Verilog: 11 circuits, main circuit RegisterFile
module CPU (
  input  in_1,
  input  in_2,
  input  in_3,
  input  [2:0] in_4,
  input  [1:0] in_5,
  input  [1:0] in_6,
  input  [1:0] in_7,
  input  [2:0] in_8,
  input  in_9,
  input  in_10,
  input  in_11,
  input  in_12,
  input  in_13,
  input  in_14,
  input  in_15,
  input  in_16,
  input  in_17,
  input  [31:0] DATA_BUS_IN,
  input  CLK,
  output [20:0] ADRESS_BUS,
  output MEM_READ,
  output MEM_WRITE,
  output [31:0] DATA_BUS_OUT
);

  wire ALUADRBUS_OUT, ALUDATBUS_OUT, comparator_1_eq, comparator_1_gt, comparator_1_lt, controlunit_1_out_5,
       IR_LD, MAR_LD, not_1_out, PC_LD, PCADRBUS_OUT, PCDATABUS_OUT, RA_SEL, RF_LD, RST;
  wire [1:0] ALUFUN_SEL, PCDATA_SEL, PCMODE_SEL;
  wire [2:0] BBUS_SEL, PCCOND_SEL;
  wire [3:0] ir_1_alufunction, multiplexer_3_out;
  wire [4:0] ir_1_ra, ir_1_rb, ir_1_rc, multiplexer_1_out, multiplexer_2_out;
  wire [5:0] ir_1_opcode;
  wire [10:0] ir_1_xtdopcode;
  wire [15:0] ir_1_offset;
  wire [20:0] ir_1_address;
  wire [31:0] alu_1_output, bit_extender_1_out, bit_extender_2_out, bit_extender_3_out,
       controlled_buffer_13_out, controlled_buffer_14_out, controlunit_1_q, ir_1_q, MAR_q, multiplexer_4_out,
       multiplexer_5_out, pc_1_q, random_1_out, registerfile_1_output__1, registerfile_1_output__2;
  wire [31:23] controlled_buffer_6_out;

  assign IR_LD = in_17 ? in_1 : 1'bz;  // Controlled_Buffer controlled_buffer_1
  // Probe on ir_1_xtdopcode
  // Probe on ir_1_opcode
  assign RA_SEL = in_17 ? in_2 : 1'bz;  // Controlled_Buffer controlled_buffer_2
  ControlUnit controlunit_1 (
    .OpCode(ir_1_opcode), .XtdOpCode(ir_1_xtdopcode), .Clk(CLK), ._0(RST), .Q(controlunit_1_q),
    .out_5(controlunit_1_out_5));
  IR ir_1 (
    .D(controlled_buffer_14_out), .OpCode(ir_1_opcode), .RA(ir_1_ra), .RB(ir_1_rb), .RC(ir_1_rc),
    .Address(ir_1_address), .Offset(ir_1_offset), .XtdOpCode(ir_1_xtdopcode), .AluFunction(ir_1_alufunction),
    .Enable(IR_LD), .Clock(CLK), .Q(ir_1_q));
  assign RF_LD = in_17 ? in_3 : 1'bz;  // Controlled_Buffer controlled_buffer_3
  assign bit_extender_1_out = {{11{1'b0}}, ir_1_address};  // Bit_Extender bit_extender_1
  assign BBUS_SEL = in_17 ? in_4 : 3'bz;  // Controlled_Buffer controlled_buffer_4
  LED led_1 (.in(controlunit_1_out_5));
  // Probe on ir_1_q
  // Probe on ir_1_ra
  // Probe on multiplexer_1_out
  Multiplexer #(.width(5), .enable("false")) multiplexer_1 (
    .in0(ir_1_rb), .in1(ir_1_ra), .out(multiplexer_1_out), .sel(RA_SEL));
  // Probe on multiplexer_2_out
  Multiplexer #(.width(5), .enable("false")) multiplexer_2 (
    .in0(ir_1_rc), .in1(ir_1_rb), .out(multiplexer_2_out), .sel(RA_SEL));
  // Probe on controlled_buffer_14_out
  assign ALUFUN_SEL = in_17 ? in_5 : 2'bz;  // Controlled_Buffer controlled_buffer_5
  assign {controlled_buffer_6_out, IR_LD, RA_SEL, RF_LD, BBUS_SEL, ALUFUN_SEL, PCDATA_SEL, PCMODE_SEL, PCCOND_SEL, PC_LD, ALUADRBUS_OUT, ALUDATBUS_OUT, PCADRBUS_OUT, PCDATABUS_OUT, MAR_LD, MEM_WRITE, MEM_READ} = not_1_out ? controlunit_1_q : 32'bz;  // Controlled_Buffer controlled_buffer_6
  not not_1 (not_1_out, in_17);
  Button Reset (.out(RST));
  RegisterFile registerfile_1 (
    .Data(controlled_buffer_14_out), .Write_Selector(ir_1_ra), .Write_Enable(RF_LD),
    .Output__1(registerfile_1_output__1), .Output__2(registerfile_1_output__2),
    .Read__1_Selector(multiplexer_1_out), .Clock(CLK), .Read__2_Selector(multiplexer_2_out));
  assign PCDATA_SEL = in_17 ? in_6 : 2'bz;  // Controlled_Buffer controlled_buffer_7
  // Probe on registerfile_1_output__1
  // Probe on registerfile_1_output__2
  assign bit_extender_2_out = {{16{1'b0}}, ir_1_offset};  // Bit_Extender bit_extender_2
  assign bit_extender_3_out = {{16{ir_1_offset[15]}}, ir_1_offset};  // Bit_Extender bit_extender_3
  assign PCMODE_SEL = in_17 ? in_7 : 2'bz;  // Controlled_Buffer controlled_buffer_8
  // Probe on {controlled_buffer_6_out, IR_LD, RA_SEL, RF_LD, BBUS_SEL, ALUFUN_SEL, PCDATA_SEL, PCMODE_SEL, PCCOND_SEL, PC_LD, ALUADRBUS_OUT, ALUDATBUS_OUT, PCADRBUS_OUT, PCDATABUS_OUT, MAR_LD, MEM_WRITE, MEM_READ}
  Random #(.width(32)) random_1 (.clk(CLK), .out(random_1_out));  // open: next, clr
  // Probe on bit_extender_1_out
  // Probe on bit_extender_3_out
  Multiplexer #(.select(2), .width(4), .enable("false")) multiplexer_3 (
    .in0(ir_1_alufunction), .in1(4'b0001), .in2(4'b1110), .in3(4'b1111), .out(multiplexer_3_out),
    .sel(ALUFUN_SEL));
  Multiplexer #(.select(3), .width(32), .enable("false")) multiplexer_4 (
    .in0(registerfile_1_output__2), .in1(bit_extender_2_out), .in2(bit_extender_3_out),
    .in3(bit_extender_1_out), .in4({32{1'b0}}), .in5({32{1'b0}}), .in6({32{1'b0}}), .in7(random_1_out),
    .out(multiplexer_4_out), .sel(BBUS_SEL));
  Multiplexer #(.select(2), .width(32), .enable("false")) multiplexer_5 (
    .in0(alu_1_output), .in1(bit_extender_1_out), .in2(bit_extender_3_out), .in3({32{1'b0}}),
    .out(multiplexer_5_out), .sel(PCDATA_SEL));
  assign PCCOND_SEL = in_17 ? in_8 : 3'bz;  // Controlled_Buffer controlled_buffer_9
  // Probe on multiplexer_3_out
  // Probe on multiplexer_4_out
  Comparator #(.width(32)) comparator_1 (
    .a(registerfile_1_output__1), .b(multiplexer_4_out), .gt(comparator_1_gt), .eq(comparator_1_eq),
    .lt(comparator_1_lt));
  assign PC_LD = in_17 ? in_9 : 1'bz;  // Controlled_Buffer controlled_buffer_10
  ALU alu_1 (
    .Input__1(registerfile_1_output__1), .Output(alu_1_output), .Input__2(multiplexer_4_out),
    .Function(multiplexer_3_out));
  PC pc_1 (
    .Address(multiplexer_5_out), .Q(pc_1_q), .Load_Select(PCMODE_SEL), .Clock(CLK),
    .Greater(comparator_1_gt), .Equal(comparator_1_eq), .Less(comparator_1_lt),
    .Condition_Select(PCCOND_SEL), .Enable(PC_LD), .Reset(RST));
  assign ALUADRBUS_OUT = in_17 ? in_10 : 1'bz;  // Controlled_Buffer controlled_buffer_11
  // Probe on pc_1_q
  // Probe on controlled_buffer_14_out
  assign ALUDATBUS_OUT = in_17 ? in_11 : 1'bz;  // Controlled_Buffer controlled_buffer_12
  // Probe on alu_1_output
  assign controlled_buffer_13_out = ALUADRBUS_OUT ? alu_1_output : 32'bz;  // Controlled_Buffer controlled_buffer_13
  assign controlled_buffer_14_out = ALUDATBUS_OUT ? alu_1_output : 32'bz;  // Controlled_Buffer controlled_buffer_14
  assign controlled_buffer_13_out = PCADRBUS_OUT ? pc_1_q : 32'bz;  // Controlled_Buffer controlled_buffer_15
  assign controlled_buffer_14_out = PCDATABUS_OUT ? pc_1_q : 32'bz;  // Controlled_Buffer controlled_buffer_16
  assign PCADRBUS_OUT = in_17 ? in_12 : 1'bz;  // Controlled_Buffer controlled_buffer_17
  // Probe on BBUS_SEL
  // Probe on ALUFUN_SEL
  Register #(.width(32)) MAR (.D(controlled_buffer_13_out), .en(MAR_LD), .Q(MAR_q), .clk(CLK));  // open: clr
  assign PCDATABUS_OUT = in_17 ? in_13 : 1'bz;  // Controlled_Buffer controlled_buffer_18
  Bit_Extender #(.in_width(32), .out_width(21)) bit_extender_4 (.in(MAR_q), .out(ADRESS_BUS));
  assign MAR_LD = in_17 ? in_14 : 1'bz;  // Controlled_Buffer controlled_buffer_19
  // Probe on PCDATA_SEL
  assign controlled_buffer_14_out = MEM_READ ? DATA_BUS_IN : 32'bz;  // Controlled_Buffer controlled_buffer_20
  assign DATA_BUS_OUT = MEM_WRITE ? controlled_buffer_14_out : 32'bz;  // Controlled_Buffer controlled_buffer_21
  assign MEM_WRITE = in_17 ? in_15 : 1'bz;  // Controlled_Buffer controlled_buffer_22
  // Probe on PCMODE_SEL
  assign MEM_READ = in_17 ? in_16 : 1'bz;  // Controlled_Buffer controlled_buffer_23
  // Probe on PCCOND_SEL

  // Other names for the same wires on the sheet: MEM_OUT = MEM_READ; MEM_LD = MEM_WRITE; CLOCK = CLK; MANUAL = in_17
endmodule

module RegisterFile (
  input  [4:0] Read__1_Selector,
  input  [31:0] Data,
  input  [4:0] Write_Selector,
  input  Write_Enable,
  input  Clock,
  input  [4:0] Read__2_Selector,
  output [31:0] Output__1,
  output [31:0] Output__2
);

  wire decoder_1_out0, decoder_1_out1, decoder_1_out2, decoder_1_out3, decoder_1_out4, decoder_1_out5,
       decoder_1_out6, decoder_1_out7, decoder_1_out8, decoder_1_out9, decoder_1_out10, decoder_1_out11,
       decoder_1_out12, decoder_1_out13, decoder_1_out14, decoder_1_out15, decoder_1_out16, decoder_1_out17,
       decoder_1_out18, decoder_1_out19, decoder_1_out20, decoder_1_out21, decoder_1_out22, decoder_1_out23,
       decoder_1_out24, decoder_1_out25, decoder_1_out26, decoder_1_out27, decoder_1_out28, decoder_1_out29,
       decoder_1_out30, decoder_1_out31;
  wire [31:0] R00out, R01out, R02out, R03out, R04out, R05out, R06out, R07out, R08out, R09out, R10out, R11out,
       R12out, R13out, R14out, R15out, R16out, R17out, R18out, R19out, R20out, R21out, R22out, R23out,
       R24out, R25out, R26out, R27out, R28out, R29out, R30out, R31out;

  Register #(.width(32)) register_1 (.D(Data), .en(decoder_1_out0), .Q(R00out), .clk(Clock));  // open: clr
  Register #(.width(32)) register_2 (.D(Data), .en(decoder_1_out1), .Q(R01out), .clk(Clock));  // open: clr
  Register #(.width(32)) register_3 (.D(Data), .en(decoder_1_out2), .Q(R02out), .clk(Clock));  // open: clr
  Register #(.width(32)) register_4 (.D(Data), .en(decoder_1_out3), .Q(R03out), .clk(Clock));  // open: clr
  Register #(.width(32)) register_5 (.D(Data), .en(decoder_1_out4), .Q(R04out), .clk(Clock));  // open: clr
  Register #(.width(32)) register_6 (.D(Data), .en(decoder_1_out5), .Q(R05out), .clk(Clock));  // open: clr
  Register #(.width(32)) register_7 (.D(Data), .en(decoder_1_out6), .Q(R06out), .clk(Clock));  // open: clr
  Register #(.width(32)) register_8 (.D(Data), .en(decoder_1_out7), .Q(R07out), .clk(Clock));  // open: clr
  // Probe on Write_Selector
  Decoder #(.select(5), .disabled(0)) decoder_1 (
    .out0(decoder_1_out0), .out1(decoder_1_out1), .out2(decoder_1_out2), .out3(decoder_1_out3),
    .out4(decoder_1_out4), .out5(decoder_1_out5), .out6(decoder_1_out6), .out7(decoder_1_out7),
    .out8(decoder_1_out8), .out9(decoder_1_out9), .out10(decoder_1_out10), .out11(decoder_1_out11),
    .out12(decoder_1_out12), .out13(decoder_1_out13), .out14(decoder_1_out14), .out15(decoder_1_out15),
    .out16(decoder_1_out16), .out17(decoder_1_out17), .out18(decoder_1_out18), .out19(decoder_1_out19),
    .out20(decoder_1_out20), .out21(decoder_1_out21), .out22(decoder_1_out22), .out23(decoder_1_out23),
    .out24(decoder_1_out24), .out25(decoder_1_out25), .out26(decoder_1_out26), .out27(decoder_1_out27),
    .out28(decoder_1_out28), .out29(decoder_1_out29), .out30(decoder_1_out30), .out31(decoder_1_out31),
    .sel(Write_Selector), .en(Write_Enable));
  Register #(.width(32)) register_9 (.D(Data), .en(decoder_1_out8), .Q(R08out), .clk(Clock));  // open: clr
  Register #(.width(32)) register_10 (.D(Data), .en(decoder_1_out9), .Q(R09out), .clk(Clock));  // open: clr
  Register #(.width(32)) register_11 (.D(Data), .en(decoder_1_out10), .Q(R10out), .clk(Clock));  // open: clr
  Register #(.width(32)) register_12 (.D(Data), .en(decoder_1_out11), .Q(R11out), .clk(Clock));  // open: clr
  Register #(.width(32)) register_13 (.D(Data), .en(decoder_1_out12), .Q(R12out), .clk(Clock));  // open: clr
  Register #(.width(32)) register_14 (.D(Data), .en(decoder_1_out13), .Q(R13out), .clk(Clock));  // open: clr
  Register #(.width(32)) register_15 (.D(Data), .en(decoder_1_out14), .Q(R14out), .clk(Clock));  // open: clr
  Register #(.width(32)) register_16 (.D(Data), .en(decoder_1_out15), .Q(R15out), .clk(Clock));  // open: clr
  Register #(.width(32)) register_17 (.D(Data), .en(decoder_1_out16), .Q(R16out), .clk(Clock));  // open: clr
  Register #(.width(32)) register_18 (.D(Data), .en(decoder_1_out17), .Q(R17out), .clk(Clock));  // open: clr
  Register #(.width(32)) register_19 (.D(Data), .en(decoder_1_out18), .Q(R18out), .clk(Clock));  // open: clr
  Register #(.width(32)) register_20 (.D(Data), .en(decoder_1_out19), .Q(R19out), .clk(Clock));  // open: clr
  Register #(.width(32)) register_21 (.D(Data), .en(decoder_1_out20), .Q(R20out), .clk(Clock));  // open: clr
  Register #(.width(32)) register_22 (.D(Data), .en(decoder_1_out21), .Q(R21out), .clk(Clock));  // open: clr
  Register #(.width(32)) register_23 (.D(Data), .en(decoder_1_out22), .Q(R22out), .clk(Clock));  // open: clr
  Register #(.width(32)) register_24 (.D(Data), .en(decoder_1_out23), .Q(R23out), .clk(Clock));  // open: clr
  Register #(.width(32)) register_25 (.D(Data), .en(decoder_1_out24), .Q(R24out), .clk(Clock));  // open: clr
  Register #(.width(32)) register_26 (.D(Data), .en(decoder_1_out25), .Q(R25out), .clk(Clock));  // open: clr
  Register #(.width(32)) register_27 (.D(Data), .en(decoder_1_out26), .Q(R26out), .clk(Clock));  // open: clr
  Register #(.width(32)) register_28 (.D(Data), .en(decoder_1_out27), .Q(R27out), .clk(Clock));  // open: clr
  Register #(.width(32)) register_29 (.D(Data), .en(decoder_1_out28), .Q(R28out), .clk(Clock));  // open: clr
  Register #(.width(32)) register_30 (.D(Data), .en(decoder_1_out29), .Q(R29out), .clk(Clock));  // open: clr
  Register #(.width(32)) register_31 (.D(Data), .en(decoder_1_out30), .Q(R30out), .clk(Clock));  // open: clr
  Register #(.width(32)) register_32 (.D(Data), .en(decoder_1_out31), .Q(R31out), .clk(Clock));  // open: clr
  Multiplexer #(.select(5), .width(32), .enable("false")) multiplexer_1 (
    .in0(R00out), .in1(R01out), .in2(R02out), .in3(R03out), .in4(R04out), .in5(R05out), .in6(R06out),
    .in7(R07out), .in8(R08out), .in9(R09out), .in10(R10out), .in11(R11out), .in12(R12out), .in13(R13out),
    .in14(R14out), .in15(R15out), .in16(R16out), .in17(R17out), .in18(R18out), .in19(R19out), .in20(R20out),
    .in21(R21out), .in22(R22out), .in23(R23out), .in24(R24out), .in25(R25out), .in26(R26out), .in27(R27out),
    .in28(R28out), .in29(R29out), .in30(R30out), .in31(R31out), .out(Output__1), .sel(Read__1_Selector));
  Multiplexer #(.select(5), .width(32), .enable("false")) multiplexer_2 (
    .in0(R00out), .in1(R01out), .in2(R02out), .in3(R03out), .in4(R04out), .in5(R05out), .in6(R06out),
    .in7(R07out), .in8(R08out), .in9(R09out), .in10(R10out), .in11(R11out), .in12(R12out), .in13(R13out),
    .in14(R14out), .in15(R15out), .in16(R16out), .in17(R17out), .in18(R18out), .in19(R19out), .in20(R20out),
    .in21(R21out), .in22(R22out), .in23(R23out), .in24(R24out), .in25(R25out), .in26(R26out), .in27(R27out),
    .in28(R28out), .in29(R29out), .in30(R30out), .in31(R31out), .out(Output__2), .sel(Read__2_Selector));
endmodule

module ALU (
  input  [3:0] Function,
  input  [31:0] Input__1,
  input  [31:0] Input__2,
  output [31:0] Output
);

  wire [4:0] bit_extender_1_out;
  wire [31:0] adder_1_out, and_1_out, divider_1_out, divider_1_rem, multiplier_1_out, negator_1_out,
       not_1_out, or_1_out, shifter_1_out, shifter_2_out, subtractor_1_out, xor_1_out;

  Subtractor #(.width(32)) subtractor_1 (.a(Input__1), .b(Input__2), .out(subtractor_1_out), .bin(1'b0));  // open: bout
  Adder #(.width(32)) adder_1 (.a(Input__1), .b(Input__2), .out(adder_1_out), .cin(1'b0));  // open: cout
  Shifter #(.width(32)) shifter_1 (.in(Input__1), .\dist (bit_extender_1_out), .out(shifter_1_out));
  Bit_Extender #(.in_width(32), .out_width(5)) bit_extender_1 (.in(Input__2), .out(bit_extender_1_out));
  Shifter #(.width(32), .shift("lr")) shifter_2 (.in(Input__1), .\dist (bit_extender_1_out), .out(shifter_2_out));
  Multiplier #(.width(32)) multiplier_1 (
    .a(Input__1), .b(Input__2), .out(multiplier_1_out), .cin({32{1'b0}}));  // open: cout
  Divider #(.width(32)) divider_1 (
    .a(Input__1), .b(Input__2), .out(divider_1_out), .upper({32{1'b0}}), .rem(divider_1_rem));
  assign and_1_out = Input__1 & Input__2;  // AND_Gate and_1, 32 bits wide
  assign or_1_out = Input__1 | Input__2;  // OR_Gate or_1, 32 bits wide
  assign xor_1_out = Input__1 ^ Input__2;  // XOR_Gate xor_1, 32 bits wide
  assign not_1_out = ~Input__1;  // NOT_Gate not_1, 32 bits wide
  Negator #(.width(32)) negator_1 (.in(Input__1), .out(negator_1_out));
  Multiplexer #(.select(4), .width(32), .enable("false")) multiplexer_1 (
    .in0(subtractor_1_out), .in1(adder_1_out), .in2(shifter_1_out), .in3(shifter_2_out),
    .in4(multiplier_1_out), .in5(divider_1_out), .in6(divider_1_rem), .in7(and_1_out), .in8(or_1_out),
    .in9(xor_1_out), .in10(not_1_out), .in11(negator_1_out), .in12({32{1'b0}}), .in13({32{1'b0}}),
    .in14(Input__2), .in15({Input__2[15:0], {16{1'b0}}}), .out(Output), .sel(Function));
endmodule

module PC (
  input  [2:0] Condition_Select,
  input  Greater,
  input  Equal,
  input  Less,
  input  [31:0] Address,
  input  [1:0] Load_Select,
  input  Enable,
  input  Clock,
  input  Reset,
  output [31:0] Q
);

  wire and_1_out, multiplexer_2_out, not_1_out, or_1_out, or_2_out;
  wire [31:0] adder_1_out, multiplexer_1_out, multiplexer_3_out;

  or or_1 (or_1_out, Greater, Equal);
  or or_2 (or_2_out, Equal, Less);
  Multiplexer #(.width(32), .enable("false")) multiplexer_1 (
    .in0(32'h1), .in1(Address), .out(multiplexer_1_out), .sel(Load_Select[1]));
  Multiplexer #(.select(3), .enable("false")) multiplexer_2 (
    .in0(1'b1), .in1(Greater), .in2(or_1_out), .in3(Equal), .in4(or_2_out), .in5(Less), .in6(not_1_out),
    .in7(1'b0), .out(multiplexer_2_out), .sel(Condition_Select));
  not not_1 (not_1_out, Equal);
  Adder #(.width(32)) adder_1 (.a(Q), .b(multiplexer_1_out), .out(adder_1_out), .cin(1'b0));  // open: cout
  and and_1 (and_1_out, Enable, multiplexer_2_out);
  Multiplexer #(.width(32), .enable("false")) multiplexer_3 (
    .in0(adder_1_out), .in1(Address), .out(multiplexer_3_out), .sel(Load_Select[0]));
  Register #(.width(32)) register_1 (.D(multiplexer_3_out), .en(and_1_out), .Q(Q), .clk(Clock), .clr(Reset));
endmodule

module IR (
  input  [31:0] D,
  input  Enable,
  input  Clock,
  output [3:0] AluFunction,
  output [5:0] OpCode,
  output [10:0] XtdOpCode,
  output [31:0] Q,
  output [4:0] RA,
  output [4:0] RB,
  output [4:0] RC,
  output [20:0] Address,
  output [15:0] Offset
);

  wire comparator_1_eq, not_1_out;

  Multiplexer #(.width(4), .enable("false")) multiplexer_1 (
    .in0(Address[3:0]), .in1(OpCode[3:0]), .out(AluFunction), .sel(not_1_out));
  not not_1 (not_1_out, comparator_1_eq);
  Comparator #(.width(6)) comparator_1 (.a({6{1'b1}}), .b(OpCode), .eq(comparator_1_eq));  // open: gt, lt
  Register #(.width(32)) register_1 (.D(D), .en(Enable), .Q({OpCode, Q[25:21], Address}), .clk(Clock));  // open: clr

  assign Offset = Address[15:0];
  assign {Q[31:26], Q[20:0]} = {OpCode, Address};
  assign RA = Q[25:21];
  assign RB = Address[20:16];
  assign RC = Address[15:11];
  assign XtdOpCode = Address[10:0];
endmodule

module ControlUnit (
  input  [5:0] OpCode,
  input  [10:0] XtdOpCode,
  input  Clk,
  input  _0,
  output out_5,
  output [31:0] Q
);

  wire and_1_out;
  wire [7:0] bit_extender_1_out, MPC_q, multiplexer_1_out, multiplexer_2_out, rom_1_data;
  wire [31:0] rom_2_data;

  and and_1 (and_1_out, OpCode[0], OpCode[1], OpCode[2], OpCode[3], OpCode[4], OpCode[5]);
  assign bit_extender_1_out = {{2{1'b0}}, OpCode};  // Bit_Extender bit_extender_1
  Multiplexer #(.width(8), .enable("false")) multiplexer_1 (
    .in0(Q[30:23]), .in1(rom_1_data), .out(multiplexer_1_out), .sel(Q[31]));
  // Probe on multiplexer_1_out
  Multiplexer #(.width(8), .enable("false")) multiplexer_2 (
    .in0(bit_extender_1_out), .in1({2'b01, XtdOpCode[5:0]}), .out(multiplexer_2_out), .sel(and_1_out));
  // Probe on multiplexer_2_out
  Register MPC (.D(multiplexer_1_out), .Q(MPC_q), .clk(Clk), .clr(_0));  // open: en
  ROM rom_1 (.addr(multiplexer_2_out), .data(rom_1_data));  // open: sel
  ROM #(.dataWidth(32)) rom_2 (.addr(MPC_q), .data(rom_2_data));  // open: sel
  Comparator comparator_1 (.a(MPC_q), .b({8{1'b0}}), .eq(out_5));  // open: gt, lt
  Register #(.width(32), .trigger("falling")) MIR (.D(rom_2_data), .Q(Q), .clk(Clk), .clr(_0));  // open: en
  // Probe on Q[30:23]

  // Notes on the sheet:
  //   contents of rom_1 (hex, n*v repeats v):
  //   3 0 4 6 8 9 a b c d e f 10 11 12 13 14 15 16 17 18 19 1a 1b 8*0 24 24 25 25 24 24 24 25 25 25 22*0
  //   12*27 4*0 2c 2d
  //   contents of rom_2 (hex, n*v repeats v):
  //   800094 1400001 80000000 1800000 2870044 100001 3870044 288022 1f0020 2880 288880 4900008 282b80
  //   282e80 282980 282a80 282d80 282c80 2848044 3848044 205380 205680 205180 205280 205580 205480 130020
  //   138020 8*0 140020 120020 0 100020 4*0 2908044 3908044
endmodule

module LCD_CONTROLER (
  input  [4:0] A,
  input  Enable,
  input  [31:0] Din,
  input  CLK,
  input  RST,
  input  Read,
  output [31:0] out_7,
  output [31:0] out_8,
  output [31:0] out_9,
  output [31:0] out_10,
  output [31:0] out_11,
  output [31:0] out_12,
  output [31:0] out_13,
  output [31:0] out_14,
  output [31:0] out_15,
  output [31:0] out_16,
  output [31:0] out_17,
  output [31:0] out_18,
  output [31:0] out_19,
  output [31:0] out_20,
  output [31:0] out_21,
  output [31:0] out_22,
  output [31:0] out_23,
  output [31:0] out_24,
  output [31:0] out_25,
  output [31:0] out_26,
  output [31:0] out_27,
  output [31:0] out_28,
  output [31:0] out_29,
  output [31:0] out_30,
  output [31:0] out_31,
  output [31:0] out_32,
  output [31:0] out_33,
  output [31:0] out_34,
  output [31:0] out_35,
  output [31:0] out_36,
  output [31:0] out_37,
  output [31:0] out_38,
  output [31:0] Dout
);

  wire and_1_out, and_2_out, and_3_out, and_4_out, and_5_out, and_6_out, and_7_out, and_8_out, and_9_out,
       and_10_out, and_11_out, and_12_out, and_13_out, and_14_out, and_15_out, and_16_out, and_17_out,
       and_18_out, and_19_out, and_20_out, and_21_out, and_22_out, and_23_out, and_24_out, and_25_out,
       and_26_out, and_27_out, and_28_out, and_29_out, and_30_out, and_31_out, and_32_out, decoder_1_out0,
       decoder_1_out1, decoder_1_out2, decoder_1_out3, decoder_1_out4, decoder_1_out5, decoder_1_out6,
       decoder_1_out7, decoder_1_out8, decoder_1_out9, decoder_1_out10, decoder_1_out11, decoder_1_out12,
       decoder_1_out13, decoder_1_out14, decoder_1_out15, decoder_1_out16, decoder_1_out17, decoder_1_out18,
       decoder_1_out19, decoder_1_out20, decoder_1_out21, decoder_1_out22, decoder_1_out23, decoder_1_out24,
       decoder_1_out25, decoder_1_out26, decoder_1_out27, decoder_1_out28, decoder_1_out29, decoder_1_out30,
       decoder_1_out31;

  Decoder #(.select(5), .enable("false")) decoder_1 (
    .out0(decoder_1_out0), .out1(decoder_1_out1), .out2(decoder_1_out2), .out3(decoder_1_out3),
    .out4(decoder_1_out4), .out5(decoder_1_out5), .out6(decoder_1_out6), .out7(decoder_1_out7),
    .out8(decoder_1_out8), .out9(decoder_1_out9), .out10(decoder_1_out10), .out11(decoder_1_out11),
    .out12(decoder_1_out12), .out13(decoder_1_out13), .out14(decoder_1_out14), .out15(decoder_1_out15),
    .out16(decoder_1_out16), .out17(decoder_1_out17), .out18(decoder_1_out18), .out19(decoder_1_out19),
    .out20(decoder_1_out20), .out21(decoder_1_out21), .out22(decoder_1_out22), .out23(decoder_1_out23),
    .out24(decoder_1_out24), .out25(decoder_1_out25), .out26(decoder_1_out26), .out27(decoder_1_out27),
    .out28(decoder_1_out28), .out29(decoder_1_out29), .out30(decoder_1_out30), .out31(decoder_1_out31),
    .sel(A));
  and and_1 (and_1_out, Enable, decoder_1_out0);
  and and_2 (and_2_out, Enable, decoder_1_out1);
  and and_3 (and_3_out, Enable, decoder_1_out3);
  and and_4 (and_4_out, Enable, decoder_1_out2);
  and and_5 (and_5_out, Enable, decoder_1_out4);
  and and_6 (and_6_out, Enable, decoder_1_out5);
  and and_7 (and_7_out, Enable, decoder_1_out6);
  and and_8 (and_8_out, Enable, decoder_1_out7);
  and and_9 (and_9_out, Enable, decoder_1_out8);
  and and_10 (and_10_out, Enable, decoder_1_out9);
  and and_11 (and_11_out, Enable, decoder_1_out11);
  and and_12 (and_12_out, Enable, decoder_1_out10);
  and and_13 (and_13_out, Enable, decoder_1_out12);
  and and_14 (and_14_out, Enable, decoder_1_out13);
  and and_15 (and_15_out, Enable, decoder_1_out14);
  and and_16 (and_16_out, Enable, decoder_1_out15);
  and and_17 (and_17_out, Enable, decoder_1_out16);
  and and_18 (and_18_out, Enable, decoder_1_out17);
  and and_19 (and_19_out, Enable, decoder_1_out19);
  and and_20 (and_20_out, Enable, decoder_1_out18);
  and and_21 (and_21_out, Enable, decoder_1_out20);
  and and_22 (and_22_out, Enable, decoder_1_out21);
  and and_23 (and_23_out, Enable, decoder_1_out22);
  and and_24 (and_24_out, Enable, decoder_1_out23);
  and and_25 (and_25_out, Enable, decoder_1_out24);
  and and_26 (and_26_out, Enable, decoder_1_out25);
  and and_27 (and_27_out, Enable, decoder_1_out27);
  and and_28 (and_28_out, Enable, decoder_1_out26);
  and and_29 (and_29_out, Enable, decoder_1_out28);
  and and_30 (and_30_out, Enable, decoder_1_out29);
  and and_31 (and_31_out, Enable, decoder_1_out30);
  and and_32 (and_32_out, Enable, decoder_1_out31);
  Register #(.width(32)) register_1 (.D(Din), .en(and_2_out), .Q(out_8), .clk(CLK), .clr(RST));
  Register #(.width(32)) register_2 (.D(Din), .en(and_3_out), .Q(out_10), .clk(CLK), .clr(RST));
  Register #(.width(32)) register_3 (.D(Din), .en(and_6_out), .Q(out_12), .clk(CLK), .clr(RST));
  Register #(.width(32)) register_4 (.D(Din), .en(and_8_out), .Q(out_14), .clk(CLK), .clr(RST));
  Register #(.width(32)) register_5 (.D(Din), .en(and_10_out), .Q(out_16), .clk(CLK), .clr(RST));
  Register #(.width(32)) register_6 (.D(Din), .en(and_11_out), .Q(out_18), .clk(CLK), .clr(RST));
  Register #(.width(32)) register_7 (.D(Din), .en(and_14_out), .Q(out_20), .clk(CLK), .clr(RST));
  Register #(.width(32)) register_8 (.D(Din), .en(and_16_out), .Q(out_22), .clk(CLK), .clr(RST));
  Register #(.width(32)) register_9 (.D(Din), .en(and_18_out), .Q(out_24), .clk(CLK), .clr(RST));
  Register #(.width(32)) register_10 (.D(Din), .en(and_19_out), .Q(out_26), .clk(CLK), .clr(RST));
  Register #(.width(32)) register_11 (.D(Din), .en(and_22_out), .Q(out_28), .clk(CLK), .clr(RST));
  Register #(.width(32)) register_12 (.D(Din), .en(and_24_out), .Q(out_30), .clk(CLK), .clr(RST));
  Register #(.width(32)) register_13 (.D(Din), .en(and_26_out), .Q(out_32), .clk(CLK), .clr(RST));
  Register #(.width(32)) register_14 (.D(Din), .en(and_27_out), .Q(out_34), .clk(CLK), .clr(RST));
  Register #(.width(32)) register_15 (.D(Din), .en(and_30_out), .Q(out_36), .clk(CLK), .clr(RST));
  Register #(.width(32)) register_16 (.D(Din), .en(and_32_out), .Q(out_38), .clk(CLK), .clr(RST));
  Register #(.width(32)) register_17 (.D(Din), .en(and_1_out), .Q(out_7), .clk(CLK), .clr(RST));
  Register #(.width(32)) register_18 (.D(Din), .en(and_4_out), .Q(out_9), .clk(CLK), .clr(RST));
  Register #(.width(32)) register_19 (.D(Din), .en(and_5_out), .Q(out_11), .clk(CLK), .clr(RST));
  Register #(.width(32)) register_20 (.D(Din), .en(and_7_out), .Q(out_13), .clk(CLK), .clr(RST));
  Register #(.width(32)) register_21 (.D(Din), .en(and_9_out), .Q(out_15), .clk(CLK), .clr(RST));
  Register #(.width(32)) register_22 (.D(Din), .en(and_12_out), .Q(out_17), .clk(CLK), .clr(RST));
  Register #(.width(32)) register_23 (.D(Din), .en(and_13_out), .Q(out_19), .clk(CLK), .clr(RST));
  Register #(.width(32)) register_24 (.D(Din), .en(and_15_out), .Q(out_21), .clk(CLK), .clr(RST));
  Register #(.width(32)) register_25 (.D(Din), .en(and_17_out), .Q(out_23), .clk(CLK), .clr(RST));
  Register #(.width(32)) register_26 (.D(Din), .en(and_20_out), .Q(out_25), .clk(CLK), .clr(RST));
  Register #(.width(32)) register_27 (.D(Din), .en(and_21_out), .Q(out_27), .clk(CLK), .clr(RST));
  Register #(.width(32)) register_28 (.D(Din), .en(and_23_out), .Q(out_29), .clk(CLK), .clr(RST));
  Register #(.width(32)) register_29 (.D(Din), .en(and_25_out), .Q(out_31), .clk(CLK), .clr(RST));
  Register #(.width(32)) register_30 (.D(Din), .en(and_28_out), .Q(out_33), .clk(CLK), .clr(RST));
  Register #(.width(32)) register_31 (.D(Din), .en(and_29_out), .Q(out_35), .clk(CLK), .clr(RST));
  Register #(.width(32)) register_32 (.D(Din), .en(and_31_out), .Q(out_37), .clk(CLK), .clr(RST));
  Multiplexer #(.select(5), .width(32)) multiplexer_1 (
    .in0(out_7), .in1(out_8), .in2(out_9), .in3(out_10), .in4(out_11), .in5(out_12), .in6(out_13),
    .in7(out_14), .in8(out_15), .in9(out_16), .in10(out_17), .in11(out_18), .in12(out_19), .in13(out_20),
    .in14(out_21), .in15(out_22), .in16(out_23), .in17(out_24), .in18(out_25), .in19(out_26), .in20(out_27),
    .in21(out_28), .in22(out_29), .in23(out_30), .in24(out_31), .in25(out_32), .in26(out_33), .in27(out_34),
    .in28(out_35), .in29(out_36), .in30(out_37), .in31(out_38), .out(Dout), .sel(A), .en(Read));
endmodule

module test (
  input  [31:0] in_1,
  input  [4:0] in_2
);

  wire button_1_out, clock_1_out, undriven;
  wire [31:0] lcd_controler_1_p6, lcd_controler_1_p7, lcd_controler_1_p8, lcd_controler_1_p9,
       lcd_controler_1_p10, lcd_controler_1_p11, lcd_controler_1_p12, lcd_controler_1_p13,
       lcd_controler_1_p14, lcd_controler_1_p15, lcd_controler_1_p16, lcd_controler_1_p17,
       lcd_controler_1_p18, lcd_controler_1_p19, lcd_controler_1_p20, lcd_controler_1_p21,
       lcd_controler_1_p22, lcd_controler_1_p23, lcd_controler_1_p24, lcd_controler_1_p25,
       lcd_controler_1_p26, lcd_controler_1_p27, lcd_controler_1_p28, lcd_controler_1_p29,
       lcd_controler_1_p30, lcd_controler_1_p31, lcd_controler_1_p32, lcd_controler_1_p33,
       lcd_controler_1_p34, lcd_controler_1_p35, lcd_controler_1_p36, lcd_controler_1_p37;

  // Probe on undriven
  Clock clock_1 (.out(clock_1_out));
  Button button_1 (.out(button_1_out));
  // LCD_CONTROLER lcd_controler_1: pin names not known; wires that end beside it: in_1, in_2, 1'b1, clock_1_out, button_1_out, lcd_controler_1_p6, lcd_controler_1_p7, lcd_controler_1_p8, lcd_controler_1_p9, lcd_controler_1_p10, lcd_controler_1_p11, lcd_controler_1_p12, lcd_controler_1_p13, lcd_controler_1_p14, lcd_controler_1_p15, lcd_controler_1_p16, lcd_controler_1_p17, lcd_controler_1_p18, lcd_controler_1_p19, lcd_controler_1_p20, lcd_controler_1_p21, lcd_controler_1_p22, lcd_controler_1_p23, lcd_controler_1_p24, lcd_controler_1_p25, lcd_controler_1_p26, lcd_controler_1_p27, lcd_controler_1_p28, lcd_controler_1_p29, lcd_controler_1_p30, lcd_controler_1_p31, lcd_controler_1_p32, lcd_controler_1_p33, lcd_controler_1_p34, lcd_controler_1_p35, lcd_controler_1_p36, lcd_controler_1_p37
  DotMatrix #(.inputtype("row"), .matrixcols(32), .matrixrows(32)) dotmatrix_1 (
    .row0(lcd_controler_1_p6), .row1(lcd_controler_1_p7), .row2(lcd_controler_1_p8),
    .row3(lcd_controler_1_p9), .row4(lcd_controler_1_p10), .row5(lcd_controler_1_p11),
    .row6(lcd_controler_1_p12), .row7(lcd_controler_1_p13), .row8(lcd_controler_1_p14),
    .row9(lcd_controler_1_p15), .row10(lcd_controler_1_p16), .row11(lcd_controler_1_p17),
    .row12(lcd_controler_1_p18), .row13(lcd_controler_1_p19), .row14(lcd_controler_1_p20),
    .row15(lcd_controler_1_p21), .row16(lcd_controler_1_p22), .row17(lcd_controler_1_p23),
    .row18(lcd_controler_1_p24), .row19(lcd_controler_1_p25), .row20(lcd_controler_1_p26),
    .row21(lcd_controler_1_p27), .row22(lcd_controler_1_p28), .row23(lcd_controler_1_p29),
    .row24(lcd_controler_1_p30), .row25(lcd_controler_1_p31), .row26(lcd_controler_1_p32),
    .row27(lcd_controler_1_p33), .row28(lcd_controler_1_p34), .row29(lcd_controler_1_p35),
    .row30(lcd_controler_1_p36), .row31(lcd_controler_1_p37));
endmodule

module Motherboard (
  input  in_1
);

  wire bit_extender_1_out, clock_1_out, cpu_1_mem_read, cpu_1_mem_write, io_controler_1_clkread,
       io_controler_1_dispread, io_controler_1_dispwrite, io_controler_1_ramread, io_controler_1_ramwrite;
  wire [4:0] bit_extender_2_out;
  wire [20:0] cpu_1_adress_bus, io_controler_1_aout;
  wire [31:0] cpu_1_data_bus_out, lcd_controler_1_out_7, lcd_controler_1_out_8, lcd_controler_1_out_9,
       lcd_controler_1_out_10, lcd_controler_1_out_11, lcd_controler_1_out_12, lcd_controler_1_out_13,
       lcd_controler_1_out_14, lcd_controler_1_out_15, lcd_controler_1_out_16, lcd_controler_1_out_17,
       lcd_controler_1_out_18, lcd_controler_1_out_19, lcd_controler_1_out_20, lcd_controler_1_out_21,
       lcd_controler_1_out_22, lcd_controler_1_out_23, lcd_controler_1_out_24, lcd_controler_1_out_25,
       lcd_controler_1_out_26, lcd_controler_1_out_27, lcd_controler_1_out_28, lcd_controler_1_out_29,
       lcd_controler_1_out_30, lcd_controler_1_out_31, lcd_controler_1_out_32, lcd_controler_1_out_33,
       lcd_controler_1_out_34, lcd_controler_1_out_35, lcd_controler_1_out_36, lcd_controler_1_out_37,
       lcd_controler_1_out_38, ram_1_data;

  Clock clock_1 (.out(clock_1_out));
  CPU cpu_1 (
    .in_17(in_1), .ADRESS_BUS(cpu_1_adress_bus), .MEM_WRITE(cpu_1_mem_write),
    .DATA_BUS_OUT(cpu_1_data_bus_out), .MEM_READ(cpu_1_mem_read), .CLK(clock_1_out), .DATA_BUS_IN(ram_1_data));  // open: in_1, in_2, in_3, in_4, in_5, in_6, in_7, in_8, in_9, in_10, in_11, in_12, in_14, in_15, in_16, in_13
  IO_Controler io_controler_1 (
    .Ain(cpu_1_adress_bus), .Read(cpu_1_mem_read), .Write(cpu_1_mem_write), .Aout(io_controler_1_aout),
    .RAMRead(io_controler_1_ramread), .RAMWrite(io_controler_1_ramwrite), .DispRead(io_controler_1_dispread),
    .DispWrite(io_controler_1_dispwrite), .ClkRead(io_controler_1_clkread));
  RAM #(.addrWidth(21), .dataWidth(32), .bus("separate")) ram_1 (
    .addr(io_controler_1_aout), .din(cpu_1_data_bus_out), .data(ram_1_data), .str(io_controler_1_ramwrite),
    .clk(clock_1_out), .ld(io_controler_1_ramread));  // open: sel, clr
  Bit_Extender #(.in_width(21), .out_width(1)) bit_extender_1 (.in(io_controler_1_aout), .out(bit_extender_1_out));
  OnChipClock onchipclock_1 (
    .A(bit_extender_1_out), .Read(io_controler_1_clkread), .out_5(ram_1_data), .Clock(clock_1_out));  // open: RST
  Bit_Extender #(.in_width(21), .out_width(5)) bit_extender_2 (.in(io_controler_1_aout), .out(bit_extender_2_out));
  LCD_CONTROLER lcd_controler_1 (
    .Enable(io_controler_1_dispwrite), .Din(cpu_1_data_bus_out), .out_7(lcd_controler_1_out_7),
    .out_8(lcd_controler_1_out_8), .out_9(lcd_controler_1_out_9), .out_10(lcd_controler_1_out_10),
    .out_11(lcd_controler_1_out_11), .out_12(lcd_controler_1_out_12), .out_13(lcd_controler_1_out_13),
    .out_14(lcd_controler_1_out_14), .out_15(lcd_controler_1_out_15), .out_16(lcd_controler_1_out_16),
    .out_17(lcd_controler_1_out_17), .out_18(lcd_controler_1_out_18), .out_19(lcd_controler_1_out_19),
    .out_20(lcd_controler_1_out_20), .out_21(lcd_controler_1_out_21), .out_22(lcd_controler_1_out_22),
    .out_23(lcd_controler_1_out_23), .out_24(lcd_controler_1_out_24), .out_25(lcd_controler_1_out_25),
    .out_26(lcd_controler_1_out_26), .out_27(lcd_controler_1_out_27), .out_28(lcd_controler_1_out_28),
    .out_29(lcd_controler_1_out_29), .out_30(lcd_controler_1_out_30), .out_31(lcd_controler_1_out_31),
    .out_32(lcd_controler_1_out_32), .out_33(lcd_controler_1_out_33), .out_34(lcd_controler_1_out_34),
    .out_35(lcd_controler_1_out_35), .out_36(lcd_controler_1_out_36), .out_37(lcd_controler_1_out_37),
    .out_38(lcd_controler_1_out_38), .A(bit_extender_2_out), .CLK(clock_1_out), .Dout(ram_1_data),
    .Read(io_controler_1_dispread));  // open: RST
  DotMatrix #(.inputtype("row"), .matrixcols(32), .matrixrows(32)) dotmatrix_1 (
    .row0(lcd_controler_1_out_7), .row1(lcd_controler_1_out_8), .row2(lcd_controler_1_out_9),
    .row3(lcd_controler_1_out_10), .row4(lcd_controler_1_out_11), .row5(lcd_controler_1_out_12),
    .row6(lcd_controler_1_out_13), .row7(lcd_controler_1_out_14), .row8(lcd_controler_1_out_15),
    .row9(lcd_controler_1_out_16), .row10(lcd_controler_1_out_17), .row11(lcd_controler_1_out_18),
    .row12(lcd_controler_1_out_19), .row13(lcd_controler_1_out_20), .row14(lcd_controler_1_out_21),
    .row15(lcd_controler_1_out_22), .row16(lcd_controler_1_out_23), .row17(lcd_controler_1_out_24),
    .row18(lcd_controler_1_out_25), .row19(lcd_controler_1_out_26), .row20(lcd_controler_1_out_27),
    .row21(lcd_controler_1_out_28), .row22(lcd_controler_1_out_29), .row23(lcd_controler_1_out_30),
    .row24(lcd_controler_1_out_31), .row25(lcd_controler_1_out_32), .row26(lcd_controler_1_out_33),
    .row27(lcd_controler_1_out_34), .row28(lcd_controler_1_out_35), .row29(lcd_controler_1_out_36),
    .row30(lcd_controler_1_out_37), .row31(lcd_controler_1_out_38));
endmodule

module IO_Controler (
  input  [20:0] Ain,
  input  Read,
  input  Write,
  output [20:0] Aout,
  output RAMRead,
  output RAMWrite,
  output DispRead,
  output DispWrite,
  output ClkRead
);

  wire comparator_1_eq, comparator_2_eq, comparator_3_eq, comparator_3_gt, comparator_4_eq, comparator_4_lt,
       or_1_out, or_2_out, or_3_out;
  wire [20:0] subtractor_1_out, subtractor_2_out;

  Comparator #(.width(21), .mode("unsigned")) comparator_1 (
    .a(Ain), .b(21'h1fffdc), .eq(comparator_1_eq));  // open: gt, lt
  Comparator #(.width(21), .mode("unsigned")) comparator_2 (
    .a(Ain), .b(21'h1fffdd), .eq(comparator_2_eq));  // open: gt, lt
  Comparator #(.width(21), .mode("unsigned")) comparator_3 (
    .a(Ain), .b(21'h1fffe0), .gt(comparator_3_gt), .eq(comparator_3_eq));  // open: lt
  Subtractor #(.width(21)) subtractor_1 (.a(Ain), .b(21'h1fffe0), .out(subtractor_1_out));  // open: bin, bout
  Comparator #(.width(21), .mode("unsigned")) comparator_4 (
    .a(Ain), .b(21'h1ffeff), .eq(comparator_4_eq), .lt(comparator_4_lt));  // open: gt
  or or_1 (or_1_out, comparator_4_eq, comparator_4_lt);
  or or_2 (or_2_out, comparator_3_gt, comparator_3_eq);
  or or_3 (or_3_out, comparator_1_eq, comparator_2_eq);
  Subtractor #(.width(21)) subtractor_2 (.a(Ain), .b(21'h1fffdc), .out(subtractor_2_out));  // open: bin, bout
  assign Aout = or_1_out ? Ain : 21'bz;  // Controlled_Buffer controlled_buffer_1
  and and_1 (RAMRead, or_1_out, Read);
  and and_2 (RAMWrite, or_1_out, Write);
  assign Aout = or_3_out ? subtractor_2_out : 21'bz;  // Controlled_Buffer controlled_buffer_2
  assign Aout = or_2_out ? subtractor_1_out : 21'bz;  // Controlled_Buffer controlled_buffer_3
  and and_3 (DispRead, or_2_out, Read);
  and and_4 (DispWrite, or_2_out, Write);
  and and_5 (ClkRead, Read, or_3_out);
endmodule

module OnChipClock (
  input  A,
  input  Read,
  input  Clock,
  input  RST,
  output [31:0] out_5
);

  wire counter_2_carry;
  wire [31:0] counter_1_q, counter_2_q;

  Counter #(.width(32), .max('hffffffff)) counter_1 (
    .count(counter_2_carry), .Q(counter_1_q), .clk(Clock), .clr(RST));  // open: load, D, carry
  Counter #(.width(32), .max('hffffffff)) counter_2 (
    .count(Clock), .Q(counter_2_q), .carry(counter_2_carry), .clk(Clock), .clr(RST));  // open: load, D
  Multiplexer #(.width(32)) multiplexer_1 (.in0(counter_2_q), .in1(counter_1_q), .out(out_5), .sel(A), .en(Read));
endmodule
